# Fritzing sketch AttinyProgrammerBoardArduinoAsISPv02 (saved by Fritzing 0.9.3b)
perfboards: 1

parts:
  Left_arduino_pin_(from_VIN) = male pin header, 8 pins [form="♂ (male)"]
  Right_arduino_pin_(from_8) = male pin header, 6 pins [form="♂ (male)"]
  Right_arduino_pin_(7) = male pin header, 1 pin [form="♂ (male)"]  # not connected
  IC_Holder = IC, DIP package, 8 pins [chip_label=ICHold]
  Capacitor_to_prevent_reset = Electrolytic Capacitor [capacitance=10µF voltage=16V package="100 mil [THT, electrolytic]"]
  J4 = male pin header, 3 pins [form="♂ (male)"]
  PullUp_reset_resistor = Resistor [tolerance=±5% resistance=10k package="2512 [SMD]"]
  Left_IC_pin = female pin header, 4 pins [form="♀ (female)"]
  Right_IC_pin = female pin header, 4 pins [form="♀ (female)"]
  Capacitor_to_stabilize = Ceramic Capacitor [capacitance="100 nF" package="0603 [SMD, multilayer]"]
  Arduino_UNO = Arduino Uno (Rev3)  # not connected
  R1 = Resistor [tolerance=±5% resistance=220 package=THT]
  LED1 = smd LED [color="Green (570nm)" package="0805 [SMD]"]

nets (from the breadboard view):
  N1: Left_arduino_pin_(from_VIN).pin2, J4.pin1
  N2: Left_arduino_pin_(from_VIN).pin3, Capacitor_to_prevent_reset.+
  N3: Left_arduino_pin_(from_VIN).pin4, J4.pin3, Capacitor_to_stabilize.1
  N4: Left_arduino_pin_(from_VIN).pin6, IC_Holder.pin4, Left_IC_pin.pin4
  N5: Left_arduino_pin_(from_VIN).pin7, Capacitor_to_prevent_reset.-, LED1.cathode
  N6: Right_arduino_pin_(from_8).pin2, IC_Holder.pin7, Right_IC_pin.pin2
  N7: Right_arduino_pin_(from_8).pin3, IC_Holder.pin6, Right_IC_pin.pin3
  N8: Right_arduino_pin_(from_8).pin4, IC_Holder.pin5, Right_IC_pin.pin4
  N9: Right_arduino_pin_(from_8).pin5, IC_Holder.pin1, PullUp_reset_resistor.Pin_1, Left_IC_pin.pin1
  N10: IC_Holder.pin2, Left_IC_pin.pin2
  N11: IC_Holder.pin3, Left_IC_pin.pin3
  N12: IC_Holder.pin8, J4.pin2, PullUp_reset_resistor.Pin_0, Right_IC_pin.pin1, Capacitor_to_stabilize.0, R1.Pin_1
  N13: R1.Pin_0, LED1.anode

notes:
  Orange: down solder
  Pink: up solder
  White/Red: wire
  Power Led
