# Fritzing sketch AttinyProgrammerBoardArduinoOriginalAsISPv01 (saved by Fritzing 0.9.3b)
perfboards: 1

parts:
  Left_arduino_pin_(from_VIN) = male pin header, 8 pins [form="♂ (male)"]
  Right_arduino_pin_(from_8) = male pin header, 6 pins [form="♂ (male)"]
  Right_arduino_pin_(7) = male pin header, 1 pin [form="♂ (male)"]  # not connected
  IC_Holder = IC, DIP package, 8 pins [chip_label=ICHold]
  Capacitor_to_prevent_reset = Electrolytic Capacitor [capacitance=10µF voltage=16V package="100 mil [THT, electrolytic]"]
  J4 = male pin header, 3 pins [form="♂ (male)"]
  PullUp_reset_resistor = Resistor [tolerance=±5% resistance=10k package="2512 [SMD]"]
  Left_IC_pin = female pin header, 4 pins [form="♀ (female)"]
  Right_IC_pin = female pin header, 4 pins [form="♀ (female)"]
  Capacitor_to_stabilize = Ceramic Capacitor [capacitance="100 nF" package="0603 [SMD, multilayer]"]
  Arduino_UNO = Arduino Uno (Rev3)

nets:
  N1: Left_arduino_pin_(from_VIN).pin3, Capacitor_to_prevent_reset.+, Arduino_UNO.RESET
  N2: Left_arduino_pin_(from_VIN).pin4, J4.pin3, Arduino_UNO.3V3
  N3: Left_arduino_pin_(from_VIN).pin5, J4.pin1, Arduino_UNO.5V
  N4: Left_arduino_pin_(from_VIN).pin6, Left_arduino_pin_(from_VIN).pin7, IC_Holder.pin4, Capacitor_to_prevent_reset.-, Left_IC_pin.pin4, Capacitor_to_stabilize.1, Arduino_UNO.GND
  N5: Right_arduino_pin_(from_8).pin2, IC_Holder.pin7, Right_IC_pin.pin2, Arduino_UNO.D13/SCK
  N6: Right_arduino_pin_(from_8).pin3, IC_Holder.pin6, Right_IC_pin.pin3, Arduino_UNO.D12/MISO
  N7: Right_arduino_pin_(from_8).pin4, IC_Holder.pin5, Right_IC_pin.pin4, Arduino_UNO.D11_PWM/MOSI
  N8: Right_arduino_pin_(from_8).pin5, IC_Holder.pin1, PullUp_reset_resistor.Pin_1, Left_IC_pin.pin1, Arduino_UNO.D10_PWM/SS
  N9: IC_Holder.pin2, Left_IC_pin.pin2
  N10: IC_Holder.pin3, Left_IC_pin.pin3
  N11: IC_Holder.pin8, J4.pin2, PullUp_reset_resistor.Pin_0, Right_IC_pin.pin1, Capacitor_to_stabilize.0

notes:
  Orange: down solder
  Pink: up solder
  White/Red: wire
  Green Wire is ArduinoUNO
  Original Patch
